# Fritzing sketch Steckplatine (saved by Fritzing 0.9.3b)
breadboards: 1

parts:
  Bauteil1 = Arduino Uno (Rev3)
  Bauteil2 = MicroSD Card Module
  Sensor_Innen = KY-033 Tracing Black White Line Hunting Sensor Module For Arduino
  Sensor_Mitte = KY-033 Tracing Black White Line Hunting Sensor Module For Arduino
  Sensor_Außen = KY-033 Tracing Black White Line Hunting Sensor Module For Arduino
  LCD2004-I2C1 = LCD2004-I2C

nets:
  N1: Bauteil1.A4/SDA, LCD2004-I2C1.SDA
  N2: Bauteil1.A5/SCL, LCD2004-I2C1.SCL
  N3: Bauteil1.D8, Sensor_Mitte.S
  N4: Bauteil1.D9_PWM, Sensor_Innen.S
  N5: Bauteil1.D11_PWM/MOSI, Bauteil2.MOSI
  N6: Bauteil1.D12/MISO, Bauteil2.MISO
  N7: Bauteil1.D13/SCK, Bauteil2.SCK
  GND: Bauteil1.GND, Bauteil2.GND, Sensor_Innen.GND, Sensor_Mitte.GND, Sensor_Außen.GND, LCD2004-I2C1.GND
  N8: Bauteil1.D5_PWM, Bauteil2.CS
  N9: Bauteil1.D7, Sensor_Außen.S
  VCC: Bauteil1.5V, Bauteil2.VCC, Sensor_Innen.V+, Sensor_Mitte.V+, Sensor_Außen.V+, LCD2004-I2C1.VCC

custom parts:
  KY-033 Tracing Black White Line Hunting Sensor Module For Arduino: Tracing Black White Line Hunting Sensor Module For Arduino Description: This is KY-033 tracking sensor. The KY-033 measures the intensity of infrared radiation and delivers it as an analog output voltage. Features: Operating voltage: 2.5 - 12V(cannot over12V) working current: 18mA-20mA at 5V Enhanced accuracy Documents: http://www.vishay.com/docs/83760/tcrt5000.pdf
  LCD2004-I2C: A standard character display with 4x20 characters. Comes in many colors with LCM2004 IIC attached.
